# Fritzing sketch Capstone_electrical (saved by Fritzing 1.0.3b)

parts:
  Arduino_CNC_Shield_V3_00_1 = Arduino_CNC_V3.00
  Part1 = Arduino Uno (Rev3)  # not connected
  Y_Axis = Stepper Motor - Unipolar
  Z_Axis = Stepper Motor - Unipolar
  X_Axis = Stepper Motor - Unipolar
  24V_-_24V = LM2596 step down module
  24V_-_12V = LM2596 step down module
  24V_-_5V = LM2596 step down module
  X_limit_switch = JL012-13-5.2 Lever (Limit) Switch SPDT + NO + NC [part_number=JL012-13-5.2]
  Y_limit_switch = JL012-13-5.2 Lever (Limit) Switch SPDT + NO + NC [part_number=JL012-13-5.2]
  Z_limit_switch = JL012-13-5.2 Lever (Limit) Switch SPDT + NO + NC [part_number=JL012-13-5.2]
  PI_Camera = Rasberry Pi NIOR Camera [chip_label=IC package="DIP (Dual Inline) [THT]"]  # not connected
  USBTTL1 = USB A Plug  # not connected
  USBTTL2 = Micro USB B Plug  # not connected
  Part2 = Adafruit Micro USB Breakout [part_number="Adafruit #1833"]
  E-Stop = Round Pushbutton
  Ring_Light = LEDs [package=led10mm]
  V1 = AC Power [voltage=5V amplitude=5V frequency=60Hz offset_voltage=0V delay_time=0s damping_factor=0s-1 phase=0degrees internal_resistance=0.1Ω]
  A2 = S-350-60 Power Supply [part_number=S-350-60 package=THT]
  Mod1 = Raspberry Pi 4B  # not connected

nets:
  GND: Arduino_CNC_Shield_V3_00_1.POWER_-, 24V_-_24V.IN-, 24V_-_24V.OUT-, 24V_-_12V.IN-, 24V_-_12V.OUT-, 24V_-_5V.IN-, 24V_-_5V.OUT-, Part2.GND, Ring_Light.C, V1.V-, A2.GND
  N1: Arduino_CNC_Shield_V3_00_1.POWER_+, 24V_-_24V.OUT+
  N2: Arduino_CNC_Shield_V3_00_1.X-MTR_'1', X_Axis.A
  N3: Arduino_CNC_Shield_V3_00_1.X-MTR_'2', X_Axis.C
  N4: Arduino_CNC_Shield_V3_00_1.X-MTR_'3', X_Axis.B
  N5: Arduino_CNC_Shield_V3_00_1.X-MTR_'4', X_Axis.D
  N6: Arduino_CNC_Shield_V3_00_1.Z-MTR_'1', Z_Axis.A
  N7: Arduino_CNC_Shield_V3_00_1.Z-MTR_'2', Z_Axis.C
  N8: Arduino_CNC_Shield_V3_00_1.Z-MTR_'3', Z_Axis.B
  N9: Arduino_CNC_Shield_V3_00_1.Z-MTR_'4', Z_Axis.D
  N10: Arduino_CNC_Shield_V3_00_1.Y-MTR_'1', Y_Axis.A
  N11: Arduino_CNC_Shield_V3_00_1.Y-MTR_'2', Y_Axis.C
  N12: Arduino_CNC_Shield_V3_00_1.Y-MTR_'3', Y_Axis.B
  N13: Arduino_CNC_Shield_V3_00_1.Y-MTR_'4', Y_Axis.D
  N14: Arduino_CNC_Shield_V3_00_1.End_Stops_Z+_(and_Z-)_/_SpnEn, Z_limit_switch.C
  N15: Arduino_CNC_Shield_V3_00_1.End_Stops_Z+_(Gnd), Z_limit_switch.NC
  N16: Arduino_CNC_Shield_V3_00_1.End_Stops_Y+_(and_Y-), Y_limit_switch.C
  N17: Arduino_CNC_Shield_V3_00_1.End_Stops_Y+_(Gnd), Y_limit_switch.NC
  N18: Arduino_CNC_Shield_V3_00_1.End_Stops_X+_(and_X-), X_limit_switch.C
  N19: Arduino_CNC_Shield_V3_00_1.End_Stops_X+_(Gnd), X_limit_switch.NC
  N20: 24V_-_12V.OUT+, Ring_Light.A
  N21: 24V_-_5V.IN+, A2.+V3
  N22: 24V_-_5V.OUT+, Part2.VBUS
  N23: E-Stop.leg0, V1.V+
  N24: E-Stop.leg1, A2.L

custom parts:
  Arduino_CNC_V3.00: Protoneer Arduino CNC Shield V3.00 If using Grbl V0.9: The “A” axis can not be used (yet). The “SCL” (Arduino A5) pin is now used for 'Probing' input. The “End Stops Z+ & Z-” (Arduino D11) and “SpnEn” (Arduino D12) have been switched!
  LM2596 step down module: LM2596 DC-DC step down power supply module 3 A.
  JL012-13-5.2 Lever (Limit) Switch SPDT + NO + NC: Micro Switch; Model No.: JL012-13.5-2; Actuator Action: Momentary; Actuator Type: Hinge Lever; Contact Configuration: 1NO, 1NC (SPDT) Temperature -25~65℃；Relative humidity: below 85%; Rate Voltage: 125V AC; Rated Current: 1A.
  Rasberry Pi NIOR Camera: Camera
  Adafruit Micro USB Breakout: Simple but effective - this breakout board has a USB Micro-B connector, with all 5 pins broken out. Great for pairing with a microcontroller with USB support, or adding USB 5V power to a project. We use a micro-AB connector with through-hole shielding pads for an excellent strong connection - it won't rip off by accident! Comes with one fully assembled and tested micro B breakout PCB and a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
  Round Pushbutton: A generic pushbutton.
  S-350-60 Power Supply: 350W Stepper motor power supply. June 2024 clean up errors in the part.
